// Logisim project LAB1_RAI_2306152393_ArzakaRaffanMawardi.circ as structural Verilog: 2 circuits, main circuit ORGate
module ORGate (
  input  IN1,
  input  IN2,
  output OUT1
);

  wire and_1_out, not_1_out, not_2_out;

  not not_1 (not_1_out, IN1);
  not not_2 (not_2_out, IN2);
  and and_1 (and_1_out, not_1_out, not_2_out);
  not not_3 (OUT1, and_1_out);
endmodule

module Rangkaian (
  input  A,
  input  B,
  input  C,
  output F
);

  wire and_1_out, and_2_out, and_3_out, and_4_out, not_1_out, not_2_out, not_3_out, orgate_1_out1,
       orgate_3_out1;

  not not_1 (not_1_out, A);
  not not_2 (not_2_out, B);
  ORGate orgate_1 (.IN1(A), .IN2(B), .OUT1(orgate_1_out1));
  and and_1 (and_1_out, B, not_1_out);
  and and_2 (and_2_out, not_2_out, A);
  not not_3 (not_3_out, C);
  and and_3 (and_3_out, C, orgate_1_out1);
  and and_4 (and_4_out, and_2_out, not_3_out);
  ORGate orgate_2 (.IN1(orgate_3_out1), .IN2(and_1_out), .OUT1(F));
  ORGate orgate_3 (.IN1(and_3_out), .IN2(and_4_out), .OUT1(orgate_3_out1));
endmodule
