// Logisim project LAB3_RAI_2306152393_ArzakaRaffanMawardi.circ as structural Verilog: 1 circuit, main circuit Code_Converter
module Code_Converter (
  input  A,
  input  B,
  input  C,
  input  D,
  output W,
  output X,
  output Y,
  output Z
);

  wire nor_1_out, nor_2_out, nor_4_out, nor_5_out, nor_6_out, nor_7_out, nor_8_out, nor_9_out, nor_10_out,
       nor_11_out, nor_12_out, nor_13_out, nor_14_out, nor_15_out, nor_16_out, nor_17_out, nor_18_out,
       nor_19_out, nor_20_out, nor_21_out, nor_22_out, nor_23_out, nor_24_out, nor_25_out, nor_26_out,
       nor_27_out, nor_28_out, nor_29_out;

  nor nor_1 (nor_1_out, B, B);
  nor nor_2 (nor_2_out, C, C);
  nor nor_3 (Z, D, D);
  nor nor_4 (nor_4_out, C, C);
  nor nor_5 (nor_5_out, nor_4_out, nor_6_out);
  nor nor_6 (nor_6_out, B, B);
  nor nor_7 (nor_7_out, D, D);
  nor nor_8 (nor_8_out, nor_7_out, nor_9_out);
  nor nor_9 (nor_9_out, C, C);
  nor nor_10 (nor_10_out, B, A);
  nor nor_11 (nor_11_out, nor_10_out, nor_10_out);
  nor nor_12 (nor_12_out, nor_2_out, nor_2_out);
  nor nor_13 (nor_13_out, nor_12_out, nor_14_out);
  nor nor_14 (nor_14_out, nor_1_out, nor_1_out);
  nor nor_15 (nor_15_out, Z, Z);
  nor nor_16 (nor_16_out, nor_15_out, nor_17_out);
  nor nor_17 (nor_17_out, nor_1_out, nor_1_out);
  nor nor_18 (nor_18_out, D, D);
  nor nor_19 (nor_19_out, nor_18_out, nor_20_out);
  nor nor_20 (nor_20_out, nor_5_out, nor_5_out);
  nor nor_21 (nor_21_out, D, D);
  nor nor_22 (nor_22_out, nor_21_out, nor_23_out);
  nor nor_23 (nor_23_out, nor_2_out, nor_2_out);
  nor nor_24 (nor_24_out, C, C);
  nor nor_25 (nor_25_out, nor_24_out, nor_26_out);
  nor nor_26 (nor_26_out, Z, Z);
  nor nor_27 (nor_27_out, nor_8_out, nor_11_out);
  nor nor_28 (nor_28_out, nor_13_out, nor_16_out, nor_19_out);
  nor nor_29 (nor_29_out, nor_22_out, nor_25_out);
  nor nor_30 (W, nor_27_out, nor_27_out);
  nor nor_31 (X, nor_28_out, nor_28_out);
  nor nor_32 (Y, nor_29_out, nor_29_out);

  // Notes on the sheet:
  //             BC
  //   CD
  //   A + B
  //   B'C'
  //          B'D'
  //   BCD
  //   C'D
  //   CD'
  //                     B'C' + B'D' + BCD
  //   D'
  //                  A + B + CD
  //             C'D + CD'
endmodule
