// Logisim project LAB5_RAI_2306152393_ArzakaRaffanMawardi.circ as structural Verilog: 2 circuits, main circuit Combinational
module Combinational (
  input  Y2,
  input  Y1,
  input  Y0,
  input  X,
  output D2,
  output D1,
  output D0,
  output Y
);

  wire and_1_out, and_2_out, and_3_out, and_4_out, and_5_out, not_1_out, not_2_out, not_3_out, or_2_out,
       or_3_out;

  not not_1 (not_1_out, Y2);
  not not_2 (not_2_out, Y1);
  not not_3 (not_3_out, Y0);
  not not_4 (D1, X);
  and and_1 (and_1_out, Y2, not_2_out, D1);
  or or_1 (D2, and_1_out, and_2_out);
  and and_2 (and_2_out, Y1, X);
  or or_2 (or_2_out, not_1_out, Y1);
  and and_3 (and_3_out, Y1, D1);
  and and_4 (and_4_out, not_2_out, X);
  or or_3 (or_3_out, Y1, Y0);
  and and_5 (and_5_out, or_2_out, not_3_out);
  and and_6 (Y, or_3_out, Y2);
  or or_4 (D0, and_5_out, and_3_out, and_4_out);
endmodule

module Sequential (
  input  X,
  output Y
);

  wire clock_1_out, combinational_1_d0, combinational_1_d1, combinational_1_d2, D0_q, D1_q, D2_q;

  Clock clock_1 (.out(clock_1_out));
  Combinational combinational_1 (
    .Y2(D2_q), .Y1(D1_q), .Y0(D0_q), .X(X), .D2(combinational_1_d2), .D1(combinational_1_d1),
    .D0(combinational_1_d0), .Y(Y));
  D_Flip_Flop D2 (.D(combinational_1_d2), .clk(clock_1_out), .Q(D2_q));  // open: Qn, preset, reset
  D_Flip_Flop D1 (.D(combinational_1_d1), .clk(clock_1_out), .Q(D1_q));  // open: Qn, preset, reset
  D_Flip_Flop D0 (.D(combinational_1_d0), .clk(clock_1_out), .Q(D0_q));  // open: Qn, preset, reset
endmodule
