// Logisim project LAB06_RAI_2306152393_ArzakaRaffanMawardi.circ as structural Verilog: 2 circuits, main circuit Combinational
module Combinational (
  input  X,
  input  Y,
  input  Z,
  input  A,
  input  B,
  output T,
  output J,
  output K,
  output D,
  output O
);

  wire and_1_out, and_2_out, and_3_out, and_4_out, and_5_out, not_1_out, not_2_out, or_1_out, xnor_1_out;

  not not_1 (not_1_out, X);
  and and_1 (and_1_out, Y, not_2_out);
  not not_2 (not_2_out, B);
  and and_2 (and_2_out, not_1_out, not_2_out);
  or or_1 (or_1_out, Z, A);
  and and_3 (and_3_out, X, K);
  and and_4 (and_4_out, and_1_out, or_1_out);
  xnor xnor_1 (xnor_1_out, A, Z);
  and and_5 (and_5_out, X, not_2_out);
  or or_2 (K, or_1_out, B);
  or or_3 (T, and_3_out, and_4_out);
  and and_6 (J, and_2_out, or_1_out);
  and and_7 (D, not_2_out, xnor_1_out);
  and and_8 (O, and_5_out, or_1_out);
endmodule

module Sequential (
  input  in_1,
  input  in_2,
  output O
);

  wire clock_1_out, combinational_1_d, combinational_1_j, combinational_1_k, combinational_1_t, d_ff_1_q,
       j_k_ff_1_q, t_ff_1_q;

  Clock clock_1 (.out(clock_1_out));
  Combinational combinational_1 (
    .X(t_ff_1_q), .Y(j_k_ff_1_q), .Z(d_ff_1_q), .A(in_1), .B(in_2), .T(combinational_1_t),
    .J(combinational_1_j), .K(combinational_1_k), .D(combinational_1_d), .O(O));
  T_Flip_Flop t_ff_1 (.T(combinational_1_t), .clk(clock_1_out), .Q(t_ff_1_q));  // open: Qn, reset, preset
  J_K_Flip_Flop j_k_ff_1 (
    .J(combinational_1_j), .K(combinational_1_k), .clk(clock_1_out), .Q(j_k_ff_1_q));  // open: Qn, preset, reset
  D_Flip_Flop d_ff_1 (.D(combinational_1_d), .clk(clock_1_out), .Q(d_ff_1_q));  // open: Qn, preset, reset
endmodule
