// Logisim project LAB7_RAI_2306152393_ArzakaRaffanMawardi.circ as structural Verilog: 4 circuits, main circuit Combinational
module Combinational (
  input  S1,
  input  S0,
  input  At,
  input  B,
  output At1
);

  wire and_1_out, and_2_out, and_3_out, and_4_out, not_1_out, not_2_out, not_3_out, not_4_out, or_1_out,
       or_2_out, xor_1_out;

  not not_1 (not_1_out, S1);
  and and_1 (and_1_out, not_1_out, not_3_out, not_4_out);
  and and_2 (and_2_out, S1, B);
  or or_1 (or_1_out, and_1_out, and_2_out);
  not not_2 (not_2_out, S0);
  xor xor_1 (xor_1_out, S0, At);
  not not_3 (not_3_out, At);
  and and_3 (and_3_out, xor_1_out, or_2_out);
  and and_4 (and_4_out, not_2_out, or_1_out);
  or or_2 (or_2_out, S1, B);
  not not_4 (not_4_out, B);
  or or_3 (At1, and_3_out, and_4_out);
endmodule

module CombinationalWithMux (
  input  S1,
  input  S0,
  input  At,
  input  Bt,
  output out_5
);

  wire and_1_out, not_1_out, not_2_out, or_1_out, xor_1_out;

  not not_1 (not_1_out, At);
  not not_2 (not_2_out, Bt);
  xor xor_1 (xor_1_out, not_2_out, At);
  and and_1 (and_1_out, Bt, not_1_out);
  or or_1 (or_1_out, At, Bt);
  Multiplexer #(.select(2)) multiplexer_1 (
    .in0(xor_1_out), .in1(and_1_out), .in2(or_1_out), .in3(not_1_out), .out(out_5), .sel({S1, S0}));
endmodule

module WithoutMux (
  input  S1,
  input  S0,
  input  [3:0] B,
  output [3:0] out_4
);

  wire clock_1_out, combinational_1_at1, combinational_2_at1, combinational_3_at1, combinational_4_at1;

  Clock clock_1 (.out(clock_1_out));
  D_Flip_Flop A0t (.D(combinational_1_at1), .clk(clock_1_out), .Q(out_4[0]));  // open: Qn, preset, reset
  Combinational combinational_1 (.S1(S1), .S0(S0), .At(out_4[0]), .B(B[0]), .At1(combinational_1_at1));
  D_Flip_Flop A1t (.D(combinational_2_at1), .clk(clock_1_out), .Q(out_4[1]));  // open: Qn, preset, reset
  Combinational combinational_2 (.S1(S1), .S0(S0), .At(out_4[1]), .B(B[1]), .At1(combinational_2_at1));
  D_Flip_Flop A2t (.D(combinational_3_at1), .clk(clock_1_out), .Q(out_4[2]));  // open: Qn, preset, reset
  Combinational combinational_3 (.S1(S1), .S0(S0), .At(out_4[2]), .B(B[2]), .At1(combinational_3_at1));
  D_Flip_Flop A3t (.D(combinational_4_at1), .clk(clock_1_out), .Q(out_4[3]));  // open: Qn, preset, reset
  Combinational combinational_4 (.S1(S1), .S0(S0), .At(out_4[3]), .B(B[3]), .At1(combinational_4_at1));
endmodule

module WithMux (
  input  S1,
  input  S0,
  input  [3:0] B,
  output [3:0] out_4
);

  wire clock_1_out, combinationalwithmux_1_out_5, combinationalwithmux_2_out_5, combinationalwithmux_3_out_5,
       combinationalwithmux_4_out_5;

  Clock clock_1 (.out(clock_1_out));
  D_Flip_Flop d_ff_1 (.D(combinationalwithmux_1_out_5), .clk(clock_1_out), .Q(out_4[0]));  // open: Qn, preset, reset
  CombinationalWithMux combinationalwithmux_1 (
    .S1(S1), .S0(S0), .At(out_4[0]), .Bt(B[0]), .out_5(combinationalwithmux_1_out_5));
  D_Flip_Flop d_ff_2 (.D(combinationalwithmux_2_out_5), .clk(clock_1_out), .Q(out_4[1]));  // open: Qn, preset, reset
  CombinationalWithMux combinationalwithmux_2 (
    .S1(S1), .S0(S0), .At(out_4[1]), .Bt(B[1]), .out_5(combinationalwithmux_2_out_5));
  D_Flip_Flop d_ff_3 (.D(combinationalwithmux_3_out_5), .clk(clock_1_out), .Q(out_4[2]));  // open: Qn, preset, reset
  CombinationalWithMux combinationalwithmux_3 (
    .S1(S1), .S0(S0), .At(out_4[2]), .Bt(B[2]), .out_5(combinationalwithmux_3_out_5));
  D_Flip_Flop d_ff_4 (.D(combinationalwithmux_4_out_5), .clk(clock_1_out), .Q(out_4[3]));  // open: Qn, preset, reset
  CombinationalWithMux combinationalwithmux_4 (
    .S1(S1), .S0(S0), .At(out_4[3]), .Bt(B[3]), .out_5(combinationalwithmux_4_out_5));
endmodule
