// Logisim project Lab8_RAI_2306152393_ArzakaRaffanMawardi.circ as structural Verilog: 2 circuits, main circuit Modified4BitCounter
module Modified4BitCounter (
  input  Load,
  input  [3:0] I,
  input  CIock,
  input  Count,
  input  Inc2,
  input  Inc4,
  input  Inc8,
  output [3:0] O,
  output CarryOut
);

  wire and_1_out, and_2_out, and_3_out, and_4_out, and_5_out, and_6_out, and_7_out, and_8_out, and_9_out,
       and_10_out, and_11_out, and_12_out, and_13_out, and_14_out, and_15_out, and_16_out, and_17_out,
       and_18_out, not_1_out, not_2_out, not_3_out, not_4_out, or_1_out, or_2_out, or_3_out, or_4_out,
       or_5_out, or_6_out, or_7_out, xor_1_out, xor_2_out, xor_3_out, xor_4_out;

  not not_1 (not_1_out, Load);
  and and_1 (and_1_out, Load, I[0]);
  and and_2 (and_2_out, not_1_out, xor_1_out);
  and and_3 (and_3_out, Load, I[1]);
  and and_4 (and_4_out, xor_2_out, not_1_out);
  and and_5 (and_5_out, Load, I[2]);
  and and_6 (and_6_out, not_1_out, xor_3_out);
  and and_7 (and_7_out, Load, I[3]);
  and and_8 (and_8_out, not_1_out, xor_4_out);
  not not_2 (not_2_out, Inc2);
  not not_3 (not_3_out, Inc4);
  not not_4 (not_4_out, Inc8);
  or or_1 (or_1_out, and_1_out, and_2_out);
  or or_2 (or_2_out, and_3_out, and_4_out);
  or or_3 (or_3_out, and_5_out, and_6_out);
  or or_4 (or_4_out, and_7_out, and_8_out);
  and and_9 (and_9_out, Count, not_2_out, not_3_out, not_4_out);
  and and_10 (and_10_out, Count, Inc2, not_3_out, not_4_out);
  and and_11 (and_11_out, Count, Inc4, not_4_out);
  and and_12 (and_12_out, Count, Inc8);
  D_Flip_Flop d_ff_1 (.D(or_1_out), .clk(CIock), .Q(O[0]));  // open: Qn, preset, reset
  D_Flip_Flop d_ff_2 (.D(or_2_out), .clk(CIock), .Q(O[1]));  // open: Qn, preset, reset
  D_Flip_Flop d_ff_3 (.D(or_3_out), .clk(CIock), .Q(O[2]));  // open: Qn, preset, reset
  D_Flip_Flop d_ff_4 (.D(or_4_out), .clk(CIock), .Q(O[3]));  // open: Qn, preset, reset
  and and_13 (and_13_out, and_10_out, and_17_out);
  or or_5 (or_5_out, and_16_out, and_10_out);
  or or_6 (or_6_out, and_11_out, and_17_out, and_13_out);
  and and_14 (and_14_out, and_18_out, and_11_out);
  and and_15 (and_15_out, and_17_out, and_18_out, and_10_out);
  and and_16 (and_16_out, O[0], and_9_out);
  and and_17 (and_17_out, O[1], or_5_out);
  and and_18 (and_18_out, O[2], or_6_out);
  or or_7 (or_7_out, and_12_out, and_18_out, and_14_out, and_15_out);
  and and_19 (CarryOut, O[3], or_7_out);
  xor xor_1 (xor_1_out, and_9_out, O[0]);
  xor xor_2 (xor_2_out, or_5_out, O[1]);
  xor xor_3 (xor_3_out, or_6_out, O[2]);
  xor xor_4 (xor_4_out, or_7_out, O[3]);
  Hex_Digit_Display hex_digit_display_1 (.value(O));  // open: dp
endmodule

module Modified16BitCounter (
  input  [3:0] Wx,
  input  [3:0] Xx,
  input  [3:0] Yx,
  input  Load,
  input  [3:0] Zx,
  input  Count,
  input  Inc2,
  input  Inc4,
  input  Inc8,
  output [3:0] Ax,
  output [3:0] Bx,
  output [3:0] Cx,
  output [3:0] Dx
);

  wire CIock_out, modified4bitcounter_2_carryout, modified4bitcounter_3_carryout,
       modified4bitcounter_4_carryout;

  Clock CIock (.out(CIock_out));
  Modified4BitCounter modified4bitcounter_1 (
    .Load(Load), .I(Wx), .CIock(CIock_out), .Count(modified4bitcounter_2_carryout), .Inc2(1'b0), .Inc4(1'b0),
    .Inc8(1'b0), .O(Ax));  // open: CarryOut
  Modified4BitCounter modified4bitcounter_2 (
    .Load(Load), .I(Xx), .CIock(CIock_out), .Count(modified4bitcounter_3_carryout), .Inc2(1'b0), .Inc4(1'b0),
    .Inc8(1'b0), .O(Bx), .CarryOut(modified4bitcounter_2_carryout));
  Hex_Digit_Display hex_digit_display_1 (.value(Ax));  // open: dp
  Modified4BitCounter modified4bitcounter_3 (
    .Load(Load), .I(Yx), .CIock(CIock_out), .Count(modified4bitcounter_4_carryout), .Inc2(1'b0), .Inc4(1'b0),
    .Inc8(1'b0), .O(Cx), .CarryOut(modified4bitcounter_3_carryout));
  Hex_Digit_Display hex_digit_display_2 (.value(Bx));  // open: dp
  Modified4BitCounter modified4bitcounter_4 (
    .Load(Load), .I(Zx), .CIock(CIock_out), .Count(Count), .Inc2(Inc2), .Inc4(Inc4), .Inc8(Inc8), .O(Dx),
    .CarryOut(modified4bitcounter_4_carryout));
  Hex_Digit_Display hex_digit_display_3 (.value(Cx));  // open: dp
  Hex_Digit_Display hex_digit_display_4 (.value(Dx));  // open: dp
endmodule
