// Logisim project TM5_RAI_2306152393_ArzakaRaffanMawardi(1).circ as structural Verilog: 2 circuits, main circuit FullAdder
module FullAdder (
  input  X,
  input  Y,
  input  Z,
  output S,
  output C
);

  wire and_1_out, and_2_out, xor_1_out;

  xor xor_1 (xor_1_out, X, Y);
  and and_1 (and_1_out, X, Y);
  xor xor_2 (S, xor_1_out, Z);
  and and_2 (and_2_out, xor_1_out, Z);
  or or_1 (C, and_2_out, and_1_out);
endmodule

module AdderAndSubtractor (
  input  [3:0] B,
  input  [3:0] A,
  input  S,
  output [3:0] out_4
);

  wire and_1_out, fulladder_1_c, fulladder_1_s, fulladder_3_c, fulladder_3_s, fulladder_4_c, fulladder_5_c,
       fulladder_5_s, fulladder_6_c, fulladder_7_c, fulladder_7_s, fulladder_8_c, xor_1_out, xor_2_out,
       xor_3_out, xor_4_out, xor_5_out, xor_6_out;

  xor xor_1 (xor_1_out, B[3], S);
  and and_1 (and_1_out, 1'b1, fulladder_1_c);
  xor xor_2 (xor_2_out, and_1_out, 1'b0);
  FullAdder fulladder_1 (.X(A[3]), .Y(xor_1_out), .Z(fulladder_3_c), .S(fulladder_1_s), .C(fulladder_1_c));
  FullAdder fulladder_2 (.X(fulladder_1_s), .Y(xor_2_out), .Z(fulladder_4_c), .S(out_4[3]));  // open: C
  xor xor_3 (xor_3_out, B[2], S);
  FullAdder fulladder_3 (.X(A[2]), .Y(xor_3_out), .Z(fulladder_5_c), .S(fulladder_3_s), .C(fulladder_3_c));
  FullAdder fulladder_4 (.X(fulladder_3_s), .Y(xor_2_out), .Z(fulladder_6_c), .S(out_4[2]), .C(fulladder_4_c));
  xor xor_4 (xor_4_out, B[1], S);
  FullAdder fulladder_5 (.X(A[1]), .Y(xor_4_out), .Z(fulladder_7_c), .S(fulladder_5_s), .C(fulladder_5_c));
  FullAdder fulladder_6 (.X(fulladder_5_s), .Y(xor_2_out), .Z(fulladder_8_c), .S(out_4[1]), .C(fulladder_6_c));
  xor xor_5 (xor_5_out, B[0], S);
  FullAdder fulladder_7 (.X(A[0]), .Y(xor_5_out), .Z(S), .S(fulladder_7_s), .C(fulladder_7_c));
  xor xor_6 (xor_6_out, and_1_out, and_1_out);
  FullAdder fulladder_8 (.X(fulladder_7_s), .Y(xor_6_out), .Z(and_1_out), .S(out_4[0]), .C(fulladder_8_c));
endmodule
