// Logisim project TM6_RAI_2306152393_ArzakaRaffanMawardi.circ as structural Verilog: 4 circuits, main circuit Combinational_No3
module Combinational_No3 (
  input  A,
  input  B,
  input  C,
  input  X,
  output D2,
  output D1,
  output D0,
  output Y
);

  wire and_1_out, and_2_out, and_3_out, and_4_out, and_5_out, and_6_out, and_7_out, and_8_out, and_9_out,
       and_10_out, and_11_out, and_12_out, and_13_out, not_1_out, not_2_out, not_3_out, not_4_out, not_5_out,
       or_1_out, or_2_out, or_5_out, or_6_out;

  not not_1 (not_1_out, A);
  not not_2 (not_2_out, B);
  not not_3 (not_3_out, C);
  not not_4 (not_4_out, X);
  or or_1 (or_1_out, A, not_2_out, C);
  and and_1 (and_1_out, not_2_out, X, A);
  and and_2 (and_2_out, B, not_1_out, or_2_out);
  and and_3 (and_3_out, not_1_out, not_3_out);
  and and_4 (and_4_out, A, C);
  and and_5 (and_5_out, not_1_out, B);
  or or_2 (or_2_out, X, not_3_out);
  not not_5 (not_5_out, B);
  and and_6 (and_6_out, or_1_out, not_4_out);
  or or_3 (D1, and_6_out, and_7_out);
  and and_7 (and_7_out, A, not_2_out, not_3_out);
  or or_4 (D2, and_1_out, and_2_out);
  or or_5 (or_5_out, and_3_out, and_4_out, and_5_out);
  and and_8 (and_8_out, not_1_out, not_5_out);
  or or_6 (or_6_out, and_8_out, and_9_out);
  and and_9 (and_9_out, B, A);
  and and_10 (and_10_out, A, not_4_out, B);
  or or_7 (Y, and_10_out, and_11_out);
  and and_11 (and_11_out, not_1_out, C, X);
  and and_12 (and_12_out, or_5_out, not_4_out);
  or or_8 (D0, and_12_out, and_13_out);
  and and_13 (and_13_out, or_6_out, X);
endmodule

module Sequential_No3 (
  input  in_1,
  output Y
);

  wire clock_1_out, combinational_no3_1_d0, combinational_no3_1_d1, combinational_no3_1_d2, D0_q, D1_q, D2_q;

  Clock clock_1 (.out(clock_1_out));
  Combinational_No3 combinational_no3_1 (
    .A(D2_q), .B(D1_q), .C(D0_q), .X(in_1), .D2(combinational_no3_1_d2), .D1(combinational_no3_1_d1),
    .D0(combinational_no3_1_d0), .Y(Y));
  D_Flip_Flop D2 (.D(combinational_no3_1_d2), .clk(clock_1_out), .Q(D2_q));  // open: Qn, preset, reset
  D_Flip_Flop D1 (.D(combinational_no3_1_d1), .clk(clock_1_out), .Q(D1_q));  // open: Qn, preset, reset
  D_Flip_Flop D0 (.D(combinational_no3_1_d0), .clk(clock_1_out), .Q(D0_q));  // open: Qn, preset, reset
endmodule

module Combinational_No4 (
  input  A,
  input  B,
  input  C,
  input  X,
  output JA,
  output KA,
  output JB,
  output KB,
  output JC,
  output KC,
  output Y
);

  wire not_1_out, not_2_out;

  and and_1 (JA, B, C, not_1_out);
  not not_1 (not_1_out, X);
  not not_2 (not_2_out, X);
  and and_2 (JB, C, not_2_out);
  or or_1 (KB, not_2_out, C);
  not not_3 (KC, X);

  assign JC = X;
  assign KA = JA;
  assign Y = A;
endmodule

module Sequential_No4 (
  input  in_1,
  output Y
);

  wire clock_1_out, combinational_no4_1_ja, combinational_no4_1_jb, combinational_no4_1_jc,
       combinational_no4_1_ka, combinational_no4_1_kb, combinational_no4_1_kc, JK_A_q, JK_B_q, JK_C_q;

  Clock clock_1 (.out(clock_1_out));
  Combinational_No4 combinational_no4_1 (
    .A(JK_A_q), .B(JK_B_q), .C(JK_C_q), .X(in_1), .JA(combinational_no4_1_ja), .KA(combinational_no4_1_ka),
    .JB(combinational_no4_1_jb), .KB(combinational_no4_1_kb), .JC(combinational_no4_1_jc),
    .KC(combinational_no4_1_kc), .Y(Y));
  J_K_Flip_Flop JK_A (
    .J(combinational_no4_1_ja), .K(combinational_no4_1_ka), .clk(clock_1_out), .Q(JK_A_q));  // open: Qn, preset, reset
  J_K_Flip_Flop JK_B (
    .J(combinational_no4_1_jb), .K(combinational_no4_1_kb), .clk(clock_1_out), .Q(JK_B_q));  // open: Qn, preset, reset
  J_K_Flip_Flop JK_C (
    .J(combinational_no4_1_jc), .K(combinational_no4_1_kc), .clk(clock_1_out), .Q(JK_C_q));  // open: Qn, preset, reset
endmodule
