// Logisim project TM8_RAI_2306152393_ArzakaRaffanMawardi.circ as structural Verilog: 1 circuit, main circuit main
module main (
  input  E,
  output [1:0] out_2
);

  wire clock_1_out, not_1_out, or_1_out, xnor_1_out, xor_1_out;

  not not_1 (not_1_out, E);
  Clock clock_1 (.out(clock_1_out));
  or or_1 (or_1_out, out_2[0], not_1_out);
  xor xor_1 (xor_1_out, out_2[0], E);
  xnor xnor_1 (xnor_1_out, or_1_out, out_2[1]);
  D_Flip_Flop D0 (.D(xor_1_out), .clk(clock_1_out), .Q(out_2[0]));  // open: Qn, preset, reset
  D_Flip_Flop D1 (.D(xnor_1_out), .clk(clock_1_out), .Q(out_2[1]));  // open: Qn, preset, reset
endmodule
